// Logisim project ula.circ as structural Verilog
module ula_cel (
  input  a,
  input  b,
  input  Cin,
  input  [4:0] Select,
  output Cout,
  output S
);

  wire and_1_out, full_adder_1_s, nand_1_out, or_1_out, xor_1_out;

  and and_1 (and_1_out, a, b);
  or or_1 (or_1_out, a, b);
  nand nand_1 (nand_1_out, a, b);
  xor xor_1 (xor_1_out, a, b);
  full_adder full_adder_1 (.Cin(Cin), .a(a), .b(b), .s(full_adder_1_s), .Cout(Cout));
  Multiplexer #(.select(5), .enable("false")) multiplexer_1 (
    .in0(and_1_out), .in1(or_1_out), .in2(nand_1_out), .in3(xor_1_out), .in4(full_adder_1_s), .out(S),
    .sel(Select));  // open: in5, in6, in7, in8, in9, in10, in11, in12, in13, in14, in15, in16, in17, in18, in19, in20, in21, in22, in23, in24, in25, in26, in27, in28, in29, in30, in31
endmodule

module full_adder (
  input  a,
  input  b,
  input  Cin,
  output Cout,
  output s
);

  wire and_1_out, and_2_out, and_3_out, and_4_out, xor_1_out;

  xor xor_1 (xor_1_out, a, b);
  xor xor_2 (s, xor_1_out, Cin);
  and and_1 (and_1_out, ~a, b, Cin);  // AND_Gate
  and and_2 (and_2_out, a, ~b, Cin);  // AND_Gate
  and and_3 (and_3_out, a, b, ~Cin);  // AND_Gate
  and and_4 (and_4_out, a, b, Cin);
  or or_1 (Cout, and_1_out, and_2_out, and_3_out, and_4_out);
endmodule
